# Fritzing sketch diagrama (saved by Fritzing 0.9.3b)
breadboards: 1

parts:
  Componente1 = Arduino Uno (Rev3)
  LCD1 = LCD screen
  U1 = POT [package=pot_mammoth]
  R1 = Photocell (LDR) [package=THT]
  R2 = Resistor [tolerance=±5% resistance=10k package="2512 [SMD]"]
  DHT1 = Humidity and Temperature Sensor DHT11

nets:
  N1: Componente1.A0, R1.pin_1, R2.Pin_0
  N2: Componente1.D10_PWM/SS, DHT1.Data-signal
  N3: Componente1.D11_PWM/MOSI, LCD1.E
  N4: Componente1.D12/MISO, LCD1.RS
  N5: Componente1.D2, LCD1.DB7
  N6: Componente1.D3_PWM, LCD1.DB6
  N7: Componente1.D4, LCD1.DB5
  N8: Componente1.D5_PWM, LCD1.DB4
  N9: LCD1.V0, U1.A
  N10: LCD1.LED+, U1.S, R1.pin_0, DHT1.Vcc
  N11: U1.E, R2.Pin_1, DHT1.GND_2

custom parts:
  Humidity and Temperature Sensor DHT11: Digital relative humidity & temperature sensor DHT11
